// Logisim project sap-II.circ as structural Verilog: 14 circuits, main circuit main
module main (
  input  CLR,
  input  J,
  input  BO
);

  wire buffer_1_out_18, buffer_1_out_19, buffer_1_out_20, buffer_1_out_21, buffer_1_out_22, buffer_1_out_23,
       buffer_1_out_24, buffer_1_out_25, buffer_2_out_18, buffer_2_out_19, buffer_2_out_20, buffer_2_out_21,
       buffer_2_out_22, buffer_2_out_23, buffer_2_out_24, buffer_2_out_25, buffer_3_out_18, buffer_3_out_19,
       buffer_3_out_20, buffer_3_out_21, buffer_3_out_22, buffer_3_out_23, buffer_3_out_24, buffer_3_out_25,
       buffer_3_out_26, buffer_3_out_27, buffer_3_out_28, buffer_3_out_29, buffer_3_out_30, buffer_3_out_31,
       buffer_3_out_32, buffer_3_out_33, buffer_4_out_18, buffer_4_out_19, buffer_4_out_20, buffer_4_out_21,
       buffer_4_out_22, buffer_4_out_23, buffer_4_out_24, buffer_4_out_25, buffer_5_out_18, buffer_5_out_19,
       buffer_5_out_20, buffer_5_out_21, buffer_5_out_22, buffer_5_out_23, buffer_5_out_24, buffer_5_out_25,
       buffer_5_out_26, buffer_5_out_27, buffer_5_out_28, buffer_5_out_29, buffer_5_out_30, buffer_5_out_31,
       buffer_5_out_32, buffer_5_out_33, buffer_6_out_18, buffer_6_out_19, buffer_6_out_20, buffer_6_out_21,
       buffer_6_out_22, buffer_6_out_23, buffer_6_out_24, buffer_6_out_25, clk_1_out_2, crom_1_out_13,
       crom_1_out_14, crom_1_out_15, crom_1_out_16, crom_1_out_17, crom_1_out_18, crom_1_out_19,
       crom_1_out_20, crom_1_out_21, crom_1_out_22, crom_1_out_23, crom_1_out_24, crom_1_out_25, IR_o0,
       IR_out_20, IR_out_21, IR_out_22, IR_out_23, IR_out_24, IR_out_25, IR_out_26, not_1_out, not_2_out,
       not_3_out, not_4_out, not_5_out, not_6_out, not_7_out, not_8_out, not_9_out, not_10_out, not_11_out,
       not_12_out, not_13_out, not_14_out, not_15_out, pc_1_o0, pc_1_o16, pc_1_out_22, pc_1_out_23,
       pc_1_out_24, pc_1_out_25, pc_1_out_26, pc_1_out_27, pc_1_out_28, pc_1_out_29, pc_1_out_30,
       pc_1_out_31, pc_1_out_32, pc_1_out_33, pc_1_out_34, pc_1_out_35, PROM_out_17, PROM_out_18,
       PROM_out_19, PROM_out_20, PROM_out_21, PROM_out_22, PROM_out_23, PROM_out_24, RAR_o0, RAR_o16,
       RAR_out_20, RAR_out_21, RAR_out_22, RAR_out_23, RAR_out_24, RAR_out_25, RAR_out_26, RAR_out_27,
       RAR_out_28, RAR_out_29, RAR_out_30, RAR_out_31, RAR_out_32, RAR_out_33, register_2_o0,
       register_2_out_20, register_2_out_21, register_2_out_22, register_2_out_23, register_2_out_24,
       register_2_out_25, register_2_out_26, register_4_o0, register_4_out_20, register_4_out_21,
       register_4_out_22, register_4_out_23, register_4_out_24, register_4_out_25, register_4_out_26,
       sequencer_1_out_2, sequencer_1_out_3, sequencer_1_out_4, sequencer_1_out_5, transistor_1_out,
       transistor_2_out, transistor_3_out, transistor_4_out, transistor_5_out, transistor_6_out,
       transistor_7_out, transistor_8_out, transistor_9_out, transistor_10_out, transistor_11_out,
       transistor_12_out, transistor_13_out, transistor_14_out, transistor_15_out, transistor_16_out;
  wire [7:0] register_1_o0, register_3_o0, transistor_23_out;

  not not_1 (not_1_out, crom_1_out_13);
  not not_2 (not_2_out, CLR);
  not not_3 (not_3_out, J);
  not not_4 (not_4_out, crom_1_out_21);
  not not_5 (not_5_out, crom_1_out_25);
  not not_6 (not_6_out, crom_1_out_24);
  LED led_1 (.in(not_7_out));
  not not_7 (not_7_out, crom_1_out_18);
  CLK clk_1 (.HLT(crom_1_out_18), .out_2(clk_1_out_2));
  Transistor transistor_1 (.in(pc_1_o0), .out(transistor_1_out), .gate(not_1_out));
  Transistor transistor_2 (.in(pc_1_out_24), .out(transistor_2_out), .gate(not_1_out));
  Transistor transistor_3 (.in(pc_1_out_23), .out(transistor_3_out), .gate(not_1_out));
  Transistor transistor_4 (.in(pc_1_out_26), .out(transistor_4_out), .gate(not_1_out));
  Transistor transistor_5 (.in(pc_1_out_22), .out(transistor_5_out), .gate(not_1_out));
  Transistor transistor_6 (.in(pc_1_out_27), .out(transistor_6_out), .gate(not_1_out));
  Transistor transistor_7 (.in(pc_1_out_28), .out(transistor_7_out), .gate(not_1_out));
  Transistor transistor_8 (.in(pc_1_out_25), .out(transistor_8_out), .gate(not_1_out));
  PC pc_1 (
    .i0(transistor_1_out), .in_6(transistor_5_out), .in_7(transistor_3_out), .in_8(transistor_2_out),
    .in_9(transistor_8_out), .in_10(transistor_4_out), .in_11(transistor_6_out), .in_12(transistor_7_out),
    .in_13(transistor_9_out), .in_14(transistor_10_out), .in_15(transistor_13_out),
    .in_16(transistor_11_out), .in_17(transistor_12_out), .in_18(transistor_15_out),
    .in_19(transistor_14_out), .i16(transistor_16_out), .CLK(clk_1_out_2), .nCLR(not_2_out),
    .CE(crom_1_out_17), .nJ(not_3_out), .o0(pc_1_o0), .out_22(pc_1_out_22), .out_23(pc_1_out_23),
    .out_24(pc_1_out_24), .out_25(pc_1_out_25), .out_26(pc_1_out_26), .out_27(pc_1_out_27),
    .out_28(pc_1_out_28), .out_29(pc_1_out_29), .out_30(pc_1_out_30), .out_31(pc_1_out_31),
    .out_32(pc_1_out_32), .out_33(pc_1_out_33), .out_34(pc_1_out_34), .out_35(pc_1_out_35), .o16(pc_1_o16));
  Transistor transistor_9 (.in(pc_1_out_29), .out(transistor_9_out), .gate(not_1_out));
  Transistor transistor_10 (.in(pc_1_out_30), .out(transistor_10_out), .gate(not_1_out));
  Transistor transistor_11 (.in(pc_1_out_32), .out(transistor_11_out), .gate(not_1_out));
  Transistor transistor_12 (.in(pc_1_out_33), .out(transistor_12_out), .gate(not_1_out));
  Transistor transistor_13 (.in(pc_1_out_31), .out(transistor_13_out), .gate(not_1_out));
  Transistor transistor_14 (.in(pc_1_out_35), .out(transistor_14_out), .gate(not_1_out));
  Transistor transistor_15 (.in(pc_1_out_34), .out(transistor_15_out), .gate(not_1_out));
  Transistor transistor_16 (.in(pc_1_o16), .out(transistor_16_out), .gate(not_1_out));
  not not_8 (not_8_out, crom_1_out_16);
  Buffer buffer_1 (
    .i(transistor_1_out), .in_2(transistor_5_out), .in_3(transistor_3_out), .in_4(transistor_2_out),
    .in_5(transistor_8_out), .in_6(transistor_4_out), .in_7(transistor_6_out), .in_8(transistor_7_out),
    .E(crom_1_out_21), .out_18(buffer_1_out_18), .out_19(buffer_1_out_19), .out_20(buffer_1_out_20),
    .out_21(buffer_1_out_21), .out_22(buffer_1_out_22), .out_23(buffer_1_out_23), .out_24(buffer_1_out_24),
    .out_25(buffer_1_out_25));  // open: in_9, in_10, in_11, in_12, in_13, in_14, in_15, in_16, out_26, out_27, out_28, out_29, out_30, out_31, out_32, out_33
  not not_9 (not_9_out, crom_1_out_22);
  Register register_1 (
    .i0(buffer_1_out_18), .in_4(buffer_1_out_19), .in_5(buffer_1_out_20), .in_6(buffer_1_out_21),
    .in_7(buffer_1_out_22), .in_8(buffer_1_out_23), .in_9(buffer_1_out_24), .in_10(buffer_1_out_25),
    .o0(register_1_o0[0]), .out_20(register_1_o0[1]), .out_21(register_1_o0[2]), .out_22(register_1_o0[3]),
    .out_23(register_1_o0[4]), .out_24(register_1_o0[5]), .out_25(register_1_o0[6]),
    .out_26(register_1_o0[7]), .nLD(not_4_out), .CLK(clk_1_out_2));  // open: in_11, in_12, in_13, in_14, in_15, in_16, in_17, i16, out_27, out_28, out_29, out_30, out_31, out_32, out_33, o16
  not not_10 (not_10_out, crom_1_out_23);
  Buffer buffer_2 (
    .i(transistor_23_out[0]), .in_2(transistor_23_out[1]), .in_3(transistor_23_out[2]),
    .in_4(transistor_23_out[3]), .in_5(transistor_23_out[4]), .in_6(transistor_23_out[5]),
    .in_7(transistor_23_out[6]), .in_8(transistor_23_out[7]), .E(crom_1_out_24), .out_18(buffer_2_out_18),
    .out_19(buffer_2_out_19), .out_20(buffer_2_out_20), .out_21(buffer_2_out_21), .out_22(buffer_2_out_22),
    .out_23(buffer_2_out_23), .out_24(buffer_2_out_24), .out_25(buffer_2_out_25));  // open: in_9, in_10, in_11, in_12, in_13, in_14, in_15, in_16, out_26, out_27, out_28, out_29, out_30, out_31, out_32, out_33
  Register register_2 (
    .i0(buffer_2_out_18), .in_4(buffer_2_out_19), .in_5(buffer_2_out_20), .in_6(buffer_2_out_21),
    .in_7(buffer_2_out_22), .in_8(buffer_2_out_23), .in_9(buffer_2_out_24), .in_10(buffer_2_out_25),
    .o0(register_2_o0), .out_20(register_2_out_20), .out_21(register_2_out_21), .out_22(register_2_out_22),
    .out_23(register_2_out_23), .out_24(register_2_out_24), .out_25(register_2_out_25),
    .out_26(register_2_out_26), .nLD(not_6_out), .CLK(clk_1_out_2));  // open: in_11, in_12, in_13, in_14, in_15, in_16, in_17, i16, out_27, out_28, out_29, out_30, out_31, out_32, out_33, o16
  Sequencer sequencer_1 (
    .CLK(clk_1_out_2), .out_2(sequencer_1_out_2), .out_3(sequencer_1_out_3), .out_4(sequencer_1_out_4),
    .out_5(sequencer_1_out_5));
  Transistor transistor_17 (.in(register_2_out_24), .out(transistor_23_out[5]), .gate(not_10_out));
  Transistor transistor_18 (.in(register_2_out_25), .out(transistor_23_out[6]), .gate(not_10_out));
  Transistor transistor_19 (.in(register_2_out_26), .out(transistor_23_out[7]), .gate(not_10_out));
  LED LM (.in(crom_1_out_23));
  LED LMAH (.in(crom_1_out_21));
  LED DRE (.in(crom_1_out_25));
  LED LMAL (.in(crom_1_out_22));
  LED EM (.in(crom_1_out_24));
  LED u_BO (.in(crom_1_out_20));
  Transistor transistor_20 (.in(register_2_out_20), .out(transistor_23_out[1]), .gate(not_10_out));
  Transistor transistor_21 (.in(register_2_out_21), .out(transistor_23_out[2]), .gate(not_10_out));
  Transistor transistor_22 (.in(register_2_out_23), .out(transistor_23_out[4]), .gate(not_10_out));
  Transistor transistor_23 (.in(register_2_o0), .out(transistor_23_out[0]), .gate(not_10_out));
  Transistor transistor_24 (.in(register_2_out_22), .out(transistor_23_out[3]), .gate(not_10_out));
  Buffer buffer_3 (
    .i(transistor_1_out), .in_2(transistor_5_out), .in_3(transistor_3_out), .in_4(transistor_2_out),
    .in_5(transistor_8_out), .in_6(transistor_4_out), .in_7(transistor_6_out), .in_8(transistor_7_out),
    .in_9(1'b0), .in_10(1'b0), .in_11(1'b0), .in_12(1'b0), .in_13(1'b0), .in_14(1'b0), .in_15(1'b0),
    .in_16(1'b0), .E(crom_1_out_16), .out_18(buffer_3_out_18), .out_19(buffer_3_out_19),
    .out_20(buffer_3_out_20), .out_21(buffer_3_out_21), .out_22(buffer_3_out_22), .out_23(buffer_3_out_23),
    .out_24(buffer_3_out_24), .out_25(buffer_3_out_25), .out_26(buffer_3_out_26), .out_27(buffer_3_out_27),
    .out_28(buffer_3_out_28), .out_29(buffer_3_out_29), .out_30(buffer_3_out_30), .out_31(buffer_3_out_31),
    .out_32(buffer_3_out_32), .out_33(buffer_3_out_33));
  Register IR (
    .i0(buffer_3_out_18), .in_4(buffer_3_out_19), .in_5(buffer_3_out_20), .in_6(buffer_3_out_21),
    .in_7(buffer_3_out_22), .in_8(buffer_3_out_23), .in_9(buffer_3_out_24), .in_10(buffer_3_out_25),
    .in_11(buffer_3_out_26), .in_12(buffer_3_out_27), .in_13(buffer_3_out_28), .in_14(buffer_3_out_29),
    .in_15(buffer_3_out_30), .in_16(buffer_3_out_31), .in_17(buffer_3_out_32), .i16(buffer_3_out_33),
    .o0(IR_o0), .out_20(IR_out_20), .out_21(IR_out_21), .out_22(IR_out_22), .out_23(IR_out_23),
    .out_24(IR_out_24), .out_25(IR_out_25), .out_26(IR_out_26), .nLD(not_8_out), .CLK(clk_1_out_2));  // open: out_27, out_28, out_29, out_30, out_31, out_32, out_33, o16
  CROM crom_1 (
    .in_1(sequencer_1_out_2), .in_2(sequencer_1_out_3), .in_3(sequencer_1_out_4), .in_4(sequencer_1_out_5),
    .in_5(IR_o0), .in_6(IR_out_20), .in_7(IR_out_21), .in_8(IR_out_22), .in_9(IR_out_23), .in_10(IR_out_24),
    .in_11(IR_out_25), .in_12(IR_out_26), .out_13(crom_1_out_13), .out_14(crom_1_out_14),
    .out_15(crom_1_out_15), .out_16(crom_1_out_16), .out_17(crom_1_out_17), .out_18(crom_1_out_18),
    .out_19(crom_1_out_19), .out_20(crom_1_out_20), .out_21(crom_1_out_21), .out_22(crom_1_out_22),
    .out_23(crom_1_out_23), .out_24(crom_1_out_24), .out_25(crom_1_out_25));  // open: out_26, out_27, out_28
  LED PCO (.in(crom_1_out_13));
  LED PO (.in(crom_1_out_15));
  LED PCE (.in(crom_1_out_17));
  LED BI (.in(crom_1_out_19));
  LED HLT (.in(crom_1_out_18));
  LED II (.in(crom_1_out_16));
  LED PI (.in(crom_1_out_14));
  Buffer buffer_4 (
    .i(transistor_1_out), .in_2(transistor_5_out), .in_3(transistor_3_out), .in_4(transistor_2_out),
    .in_5(transistor_8_out), .in_6(transistor_4_out), .in_7(transistor_6_out), .in_8(transistor_7_out),
    .E(crom_1_out_22), .out_18(buffer_4_out_18), .out_19(buffer_4_out_19), .out_20(buffer_4_out_20),
    .out_21(buffer_4_out_21), .out_22(buffer_4_out_22), .out_23(buffer_4_out_23), .out_24(buffer_4_out_24),
    .out_25(buffer_4_out_25));  // open: in_9, in_10, in_11, in_12, in_13, in_14, in_15, in_16, out_26, out_27, out_28, out_29, out_30, out_31, out_32, out_33
  Register register_3 (
    .i0(buffer_4_out_18), .in_4(buffer_4_out_19), .in_5(buffer_4_out_20), .in_6(buffer_4_out_21),
    .in_7(buffer_4_out_22), .in_8(buffer_4_out_23), .in_9(buffer_4_out_24), .in_10(buffer_4_out_25),
    .o0(register_3_o0[0]), .out_20(register_3_o0[1]), .out_21(register_3_o0[2]), .out_22(register_3_o0[3]),
    .out_23(register_3_o0[4]), .out_24(register_3_o0[5]), .out_25(register_3_o0[6]),
    .out_26(register_3_o0[7]), .nLD(not_9_out), .CLK(clk_1_out_2));  // open: in_11, in_12, in_13, in_14, in_15, in_16, in_17, i16, out_27, out_28, out_29, out_30, out_31, out_32, out_33, o16
  RAM_part #(.addrWidth(16), .bus("asynch")) ram_1 (
    .addr({register_1_o0, register_3_o0}), .data(transistor_23_out), .sel(1'b1), .ld(not_10_out), .clr(1'b0));
  Transistor transistor_25 (.in(register_2_o0), .out(transistor_1_out), .gate(not_5_out));
  Transistor transistor_26 (.in(register_2_out_20), .out(transistor_5_out), .gate(not_5_out));
  Transistor transistor_27 (.in(register_2_out_21), .out(transistor_3_out), .gate(not_5_out));
  Transistor transistor_28 (.in(register_2_out_22), .out(transistor_2_out), .gate(not_5_out));
  Transistor transistor_29 (.in(register_2_out_23), .out(transistor_8_out), .gate(not_5_out));
  Transistor transistor_30 (.in(register_2_out_24), .out(transistor_4_out), .gate(not_5_out));
  Transistor transistor_31 (.in(register_2_out_25), .out(transistor_6_out), .gate(not_5_out));
  Transistor transistor_32 (.in(register_2_out_26), .out(transistor_7_out), .gate(not_5_out));
  LED led_2 (.in(transistor_15_out));
  LED led_3 (.in(transistor_14_out));
  LED led_4 (.in(transistor_12_out));
  LED led_5 (.in(transistor_16_out));
  LED led_6 (.in(transistor_9_out));
  LED led_7 (.in(transistor_11_out));
  LED led_8 (.in(transistor_10_out));
  LED led_9 (.in(transistor_13_out));
  LED led_10 (.in(transistor_6_out));
  LED led_11 (.in(transistor_7_out));
  LED led_12 (.in(transistor_8_out));
  LED led_13 (.in(transistor_4_out));
  LED led_14 (.in(transistor_2_out));
  LED led_15 (.in(transistor_3_out));
  LED led_16 (.in(transistor_5_out));
  LED led_17 (.in(transistor_1_out));
  not not_11 (not_11_out, not_13_out);
  not not_12 (not_12_out, crom_1_out_19);
  PROM PROM (
    .in_1(RAR_o0), .in_2(RAR_out_20), .in_3(RAR_out_21), .in_4(RAR_out_22), .in_5(RAR_out_23),
    .in_6(RAR_out_24), .in_7(RAR_out_25), .in_8(RAR_out_26), .in_9(RAR_out_27), .in_10(RAR_out_28),
    .in_11(RAR_out_29), .in_12(RAR_out_30), .in_13(RAR_out_31), .in_14(RAR_out_32), .in_15(RAR_out_33),
    .in_16(RAR_o16), .out_17(PROM_out_17), .out_18(PROM_out_18), .out_19(PROM_out_19), .out_20(PROM_out_20),
    .out_21(PROM_out_21), .out_22(PROM_out_22), .out_23(PROM_out_23), .out_24(PROM_out_24));
  Transistor transistor_33 (.in(PROM_out_23), .out(transistor_6_out), .gate(not_14_out));
  Transistor transistor_34 (.in(PROM_out_21), .out(transistor_8_out), .gate(not_14_out));
  Transistor transistor_35 (.in(PROM_out_19), .out(transistor_3_out), .gate(not_14_out));
  Transistor transistor_36 (.in(PROM_out_20), .out(transistor_2_out), .gate(not_14_out));
  Transistor transistor_37 (.in(PROM_out_17), .out(transistor_1_out), .gate(not_14_out));
  Transistor transistor_38 (.in(PROM_out_24), .out(transistor_7_out), .gate(not_14_out));
  Transistor transistor_39 (.in(PROM_out_18), .out(transistor_5_out), .gate(not_14_out));
  Transistor transistor_40 (.in(PROM_out_22), .out(transistor_4_out), .gate(not_14_out));
  Transistor transistor_41 (.in(register_4_out_24), .out(transistor_4_out), .gate(not_15_out));
  Transistor transistor_42 (.in(register_4_out_25), .out(transistor_6_out), .gate(not_15_out));
  Transistor transistor_43 (.in(register_4_out_26), .out(transistor_7_out), .gate(not_15_out));
  Transistor transistor_44 (.in(register_4_out_23), .out(transistor_8_out), .gate(not_15_out));
  Buffer buffer_5 (
    .i(transistor_1_out), .in_2(transistor_5_out), .in_3(transistor_3_out), .in_4(transistor_2_out),
    .in_5(transistor_8_out), .in_6(transistor_4_out), .in_7(transistor_6_out), .in_8(transistor_7_out),
    .in_9(transistor_9_out), .in_10(transistor_10_out), .in_11(transistor_13_out), .in_12(transistor_11_out),
    .in_13(transistor_12_out), .in_14(transistor_15_out), .in_15(transistor_14_out),
    .in_16(transistor_16_out), .E(not_11_out), .out_18(buffer_5_out_18), .out_19(buffer_5_out_19),
    .out_20(buffer_5_out_20), .out_21(buffer_5_out_21), .out_22(buffer_5_out_22), .out_23(buffer_5_out_23),
    .out_24(buffer_5_out_24), .out_25(buffer_5_out_25), .out_26(buffer_5_out_26), .out_27(buffer_5_out_27),
    .out_28(buffer_5_out_28), .out_29(buffer_5_out_29), .out_30(buffer_5_out_30), .out_31(buffer_5_out_31),
    .out_32(buffer_5_out_32), .out_33(buffer_5_out_33));
  not not_13 (not_13_out, crom_1_out_14);
  Register RAR (
    .i0(buffer_5_out_18), .in_4(buffer_5_out_19), .in_5(buffer_5_out_20), .in_6(buffer_5_out_21),
    .in_7(buffer_5_out_22), .in_8(buffer_5_out_23), .in_9(buffer_5_out_24), .in_10(buffer_5_out_25),
    .in_11(buffer_5_out_26), .in_12(buffer_5_out_27), .in_13(buffer_5_out_28), .in_14(buffer_5_out_29),
    .in_15(buffer_5_out_30), .in_16(buffer_5_out_31), .in_17(buffer_5_out_32), .i16(buffer_5_out_33),
    .o0(RAR_o0), .out_20(RAR_out_20), .out_21(RAR_out_21), .out_22(RAR_out_22), .out_23(RAR_out_23),
    .out_24(RAR_out_24), .out_25(RAR_out_25), .out_26(RAR_out_26), .out_27(RAR_out_27), .out_28(RAR_out_28),
    .out_29(RAR_out_29), .out_30(RAR_out_30), .out_31(RAR_out_31), .out_32(RAR_out_32), .out_33(RAR_out_33),
    .o16(RAR_o16), .nLD(not_13_out), .CLK(clk_1_out_2));
  not not_14 (not_14_out, crom_1_out_15);
  Buffer buffer_6 (
    .i(transistor_1_out), .in_2(transistor_5_out), .in_3(transistor_3_out), .in_4(transistor_2_out),
    .in_5(transistor_8_out), .in_6(transistor_4_out), .in_7(transistor_6_out), .in_8(transistor_7_out),
    .E(crom_1_out_19), .out_18(buffer_6_out_18), .out_19(buffer_6_out_19), .out_20(buffer_6_out_20),
    .out_21(buffer_6_out_21), .out_22(buffer_6_out_22), .out_23(buffer_6_out_23), .out_24(buffer_6_out_24),
    .out_25(buffer_6_out_25));  // open: in_9, in_10, in_11, in_12, in_13, in_14, in_15, in_16, out_26, out_27, out_28, out_29, out_30, out_31, out_32, out_33
  Register register_4 (
    .i0(buffer_6_out_18), .in_4(buffer_6_out_19), .in_5(buffer_6_out_20), .in_6(buffer_6_out_21),
    .in_7(buffer_6_out_22), .in_8(buffer_6_out_23), .in_9(buffer_6_out_24), .in_10(buffer_6_out_25),
    .o0(register_4_o0), .out_20(register_4_out_20), .out_21(register_4_out_21), .out_22(register_4_out_22),
    .out_23(register_4_out_23), .out_24(register_4_out_24), .out_25(register_4_out_25),
    .out_26(register_4_out_26), .nLD(not_12_out), .CLK(clk_1_out_2));  // open: in_11, in_12, in_13, in_14, in_15, in_16, in_17, i16, out_27, out_28, out_29, out_30, out_31, out_32, out_33, o16
  not not_15 (not_15_out, BO);
  Transistor transistor_45 (.in(register_4_out_21), .out(transistor_3_out), .gate(not_15_out));
  Transistor transistor_46 (.in(register_4_out_22), .out(transistor_2_out), .gate(not_15_out));
  Transistor transistor_47 (.in(register_4_o0), .out(transistor_1_out), .gate(not_15_out));
  Transistor transistor_48 (.in(register_4_out_20), .out(transistor_5_out), .gate(not_15_out));

  // Notes on the sheet:
  //   HLT
  //   PCO
  //   PCE
  //   CLK
  //   II
  //   CLK
  //   CLK
  //   CLK
  //   DATA REG
  //   RAM
  //   PROGRAM COUNTER
  //   INSTRUCTION
  //   ADDR REG
  //   BUS
  //   ROM
  //   B
  //   CLK
  //   PI
  //   PO
  //   BI
  //   CLK
  //   TODO,
  //   MEM
  //   Fetch Cycle
  //   STI B
  //   PC out, PROM in
  //   Instruction in, PROM out, PCE
  //   PC out, PROM In
  //   BI, PROM O, CE
endmodule

module PC (
  input  CLK,
  input  nCLR,
  input  CE,
  input  nJ,
  input  i0,
  input  in_6,
  input  in_7,
  input  in_8,
  input  in_9,
  input  in_10,
  input  in_11,
  input  in_12,
  input  in_13,
  input  in_14,
  input  in_15,
  input  in_16,
  input  in_17,
  input  in_18,
  input  in_19,
  input  i16,
  output o0,
  output out_22,
  output out_23,
  output out_24,
  output out_25,
  output out_26,
  output out_27,
  output out_28,
  output out_29,
  output out_30,
  output out_31,
  output out_32,
  output out_33,
  output out_34,
  output out_35,
  output o16
);

  wire n74161_1_p7, n74161_2_p8, n74161_3_p10;

  // _74161 74161_1: pin names not known; wires that end beside it: nCLR, CLK, i0, in_6, in_7, in_8, n74161_1_p7, o0, out_22, out_23, out_24
  // _74161 74161_2: pin names not known; wires that end beside it: nCLR, CLK, in_9, in_10, in_11, CE, nJ, n74161_2_p8, out_25, out_26, out_27
  // _74161 74161_3: pin names not known; wires that end beside it: in_12, n74161_1_p7, nCLR, CLK, in_13, in_14, in_15, out_28, nJ, n74161_3_p10, out_29, out_30, out_31
  // _74161 74161_4: pin names not known; wires that end beside it: in_16, n74161_2_p8, nCLR, CLK, in_17, in_18, in_19, i16, n74161_3_p10, out_32, nJ, out_33, out_34, out_35, o16, nJ

  // Notes on the sheet:
  //   Has 16 bits; therefore can count from 0x0000 to 0xFFFF.
  //   A low /CLR signal resets the PC.
endmodule

module Register (
  input  nLD,
  input  CLK,
  input  i0,
  input  in_4,
  input  in_5,
  input  in_6,
  input  in_7,
  input  in_8,
  input  in_9,
  input  in_10,
  input  in_11,
  input  in_12,
  input  in_13,
  input  in_14,
  input  in_15,
  input  in_16,
  input  in_17,
  input  i16,
  output o0,
  output out_20,
  output out_21,
  output out_22,
  output out_23,
  output out_24,
  output out_25,
  output out_26,
  output out_27,
  output out_28,
  output out_29,
  output out_30,
  output out_31,
  output out_32,
  output out_33,
  output o16
);

  // IC_74173 ic_74173_1: pin names not known; wires that end beside it: i0, in_4, in_5, in_6, CLK, nLD, o0, out_20, out_21, out_22
  // IC_74173 ic_74173_2: pin names not known; wires that end beside it: in_7, in_8, in_9, in_10, CLK, 1'b0, out_23, out_24, out_25, out_26
  // IC_74173 ic_74173_3: pin names not known; wires that end beside it: nLD, in_11, in_12, in_13, in_14, CLK, 1'b0, out_27, out_28, out_29, out_30
  // IC_74173 ic_74173_4: pin names not known; wires that end beside it: nLD, in_15, in_16, in_17, i16, CLK, nLD, 1'b0, 1'b0, out_31, out_32, out_33, o16
endmodule

module Buffer (
  input  i,
  input  in_2,
  input  in_3,
  input  in_4,
  input  in_5,
  input  in_6,
  input  in_7,
  input  in_8,
  input  in_9,
  input  in_10,
  input  in_11,
  input  in_12,
  input  in_13,
  input  in_14,
  input  in_15,
  input  in_16,
  input  E,
  output out_18,
  output out_19,
  output out_20,
  output out_21,
  output out_22,
  output out_23,
  output out_24,
  output out_25,
  output out_26,
  output out_27,
  output out_28,
  output out_29,
  output out_30,
  output out_31,
  output out_32,
  output out_33
);

  assign out_18 = E ? i : 1'bz;  // Controlled_Buffer controlled_buffer_1
  assign out_19 = E ? in_2 : 1'bz;  // Controlled_Buffer controlled_buffer_2
  assign out_20 = E ? in_3 : 1'bz;  // Controlled_Buffer controlled_buffer_3
  assign out_21 = E ? in_4 : 1'bz;  // Controlled_Buffer controlled_buffer_4
  assign out_22 = E ? in_5 : 1'bz;  // Controlled_Buffer controlled_buffer_5
  assign out_23 = E ? in_6 : 1'bz;  // Controlled_Buffer controlled_buffer_6
  assign out_24 = E ? in_7 : 1'bz;  // Controlled_Buffer controlled_buffer_7
  assign out_25 = E ? in_8 : 1'bz;  // Controlled_Buffer controlled_buffer_8
  assign out_26 = E ? in_9 : 1'bz;  // Controlled_Buffer controlled_buffer_9
  assign out_27 = E ? in_10 : 1'bz;  // Controlled_Buffer controlled_buffer_10
  assign out_28 = E ? in_11 : 1'bz;  // Controlled_Buffer controlled_buffer_11
  assign out_29 = E ? in_12 : 1'bz;  // Controlled_Buffer controlled_buffer_12
  assign out_30 = E ? in_13 : 1'bz;  // Controlled_Buffer controlled_buffer_13
  assign out_31 = E ? in_14 : 1'bz;  // Controlled_Buffer controlled_buffer_14
  assign out_32 = E ? in_15 : 1'bz;  // Controlled_Buffer controlled_buffer_15
  assign out_33 = E ? in_16 : 1'bz;  // Controlled_Buffer controlled_buffer_16
endmodule

// ROM
module PROM (
  input  in_1,
  input  in_2,
  input  in_3,
  input  in_4,
  input  in_5,
  input  in_6,
  input  in_7,
  input  in_8,
  input  in_9,
  input  in_10,
  input  in_11,
  input  in_12,
  input  in_13,
  input  in_14,
  input  in_15,
  input  in_16,
  output out_17,
  output out_18,
  output out_19,
  output out_20,
  output out_21,
  output out_22,
  output out_23,
  output out_24
);

  ROM #(.addrWidth(16)) rom_1 (
    .addr({in_16, in_15, in_14, in_13, in_12, in_11, in_10, in_9, in_8, in_7, in_6, in_5, in_4, in_3, in_2, in_1}),
    .data({out_24, out_23, out_22, out_21, out_20, out_19, out_18, out_17}));  // open: sel

  // Notes on the sheet:
  //   LDB #$55
  //   HLT
  //   contents of rom_1 (hex, n*v repeats v):
  //   1 55 ff
  //   01 =>LDB#(VAL)
  //   ff => HLT
endmodule

module Sequencer (
  input  CLK,
  output out_2,
  output out_3,
  output out_4,
  output out_5
);

  wire n74161_1_p1, not_1_out;

  not not_1 (not_1_out, CLK);
  // _74161 74161_1: pin names not known; wires that end beside it: n74161_1_p1, not_1_out, 1'b1, out_2, out_3, out_4, out_5
  // _74138 74138_1: pin names not known; wires that end beside it: out_2, out_3, out_4, 1'b0, 1'b1, n74161_1_p1
endmodule

// Instruction Decoder
module CROM (
  input  in_1,
  input  in_2,
  input  in_3,
  input  in_4,
  input  in_5,
  input  in_6,
  input  in_7,
  input  in_8,
  input  in_9,
  input  in_10,
  input  in_11,
  input  in_12,
  output out_13,
  output out_14,
  output out_15,
  output out_16,
  output out_17,
  output out_18,
  output out_19,
  output out_20,
  output out_21,
  output out_22,
  output out_23,
  output out_24,
  output out_25,
  output out_26,
  output out_27,
  output out_28
);

  ROM #(.addrWidth(12), .dataWidth(16)) rom_1 (
    .addr({in_12, in_11, in_10, in_9, in_8, in_7, in_6, in_5, in_4, in_3, in_2, in_1}),
    .data({out_28, out_27, out_26, out_25, out_24, out_23, out_22, out_21, out_20, out_19, out_18, out_17, out_16, out_15, out_14, out_13}));  // open: sel

  // Notes on the sheet:
  //   contents of rom_1 (hex, n*v repeats v):
  //   3 1c 14*0 3 1c 3 54 12*0 3 1c 14*0 3 1c 14*0 3 1c 14*0 3 1c 14*0 3 1c 14*0 3 1c 14*0 3 1c 14*0 3 1c
  //   14*0 3 1c 14*0 3 1c 14*0 3 1c 14*0 3 1c 14*0 3 1c 14*0 3 1c 14*0 3 1c 14*0 3 1c 14*0 3 1c 14*0 3 1c
  //   14*0 3 1c 14*0 3 1c 14*0 3 1c 14*0 3 1c 14*0 3 1c 14*0 3 1c 14*0 3 1c 14*0 3 1c 14*0 3 1c 14*0 3 1c
  //   14*0 3 1c 14*0 3 1c 14*0 3 1c 14*0 3 1c 14*0 3 1c 14*0 3 1c 14*0 3 1c 14*0 3 1c 14*0 3 1c 14*0 3 1c
  //   14*0 3 1c 14*0 3 1c 14*0 3 1c 14*0 3 1c 14*0 3 1c 14*0 3 1c 14*0 3 1c 14*0 3 1c 14*0 3 1c 14*0 3 1c
  //   14*0 3 1c 14*0 3 1c 14*0 3 1c 14*0 3 1c 14*0 3 1c 14*0 3 1c 14*0 3 1c 14*0 3 1c 14*0 3 1c 14*0 3 1c
  //   14*0 3 1c 14*0 3 1c 14*0 3 1c 14*0 3 1c 14*0 3 1c 14*0 3 1c 14*0 3 1c 14*0 3 1c 14*0 3 1c 14*0 3 1c
  //   14*0 3 1c 14*0 3 1c 2942*0 20 20 20
endmodule

module CLK (
  input  HLT,
  output out_2
);

  wire clock_1_out, not_1_out;

  Clock clock_1 (.out(clock_1_out));
  not not_1 (not_1_out, clock_1_out);
  nor nor_1 (out_2, HLT, not_1_out);
endmodule

module RAM (
  input  in_1,
  input  in_2,
  input  in_3,
  input  in_4,
  input  in_5,
  input  in_6,
  input  in_7,
  input  in_8,
  input  in_9,
  input  in_10,
  input  in_11,
  input  in_12,
  input  in_13,
  input  in_14,
  input  in_15,
  input  in_16,
  input  in_17
);

  wire not_1_out;
  wire [7:7] ram_1_data;

  RAM_part #(.addrWidth(16), .bus("asynch")) ram_1 (
    .addr({in_16, in_15, in_14, in_13, in_12, in_11, in_10, in_9, in_8, in_7, in_6, in_5, in_4, in_3, in_2, in_1}),
    .data({8{ram_1_data[7]}}), .sel(1'b1), .ld(not_1_out));  // open: clr
  not not_1 (not_1_out, in_17);
  Transistor transistor_1 (.in(1'b1), .out(ram_1_data[7]), .gate(not_1_out));
endmodule

module _8b_select (
  input  S,
  input  A0,
  input  A1,
  input  A2,
  input  A3,
  input  A4,
  input  A5,
  input  A6,
  input  A7,
  input  B0,
  input  B1,
  input  B2,
  input  B3,
  input  B4,
  input  B5,
  input  B6,
  input  B7,
  output Y0,
  output Y1,
  output Y2,
  output Y3,
  output Y4,
  output Y5,
  output Y6,
  output Y7
);

  // _74157 74157_1: pin names not known; wires that end beside it: S, A0, B0, Y1, A1, B1, Y0, 1'b0, A3, B3, Y2, A2, B2, Y3
  // _74157 74157_2: pin names not known; wires that end beside it: S, A4, B4, Y5, A5, B5, Y4, 1'b0, A7, B7, Y6, A6, B6, Y7
endmodule

module ALU (
  input  ZX,
  input  ZY,
  input  NX,
  input  NY,
  input  f,
  input  NO,
  input  X0,
  input  in_8,
  input  in_9,
  input  in_10,
  input  in_11,
  input  in_12,
  input  in_13,
  input  in_14,
  input  Y0,
  input  in_16,
  input  in_17,
  input  in_18,
  input  in_19,
  input  in_20,
  input  in_21,
  input  in_22,
  output out_23,
  output out_24,
  output out_25,
  output out_26,
  output out_27,
  output out_28,
  output out_29,
  output out_30
);

  wire n8b_1_y0, n8b_1_y1, n8b_1_y2, n8b_1_y3, n8b_1_y4, n8b_1_y5, n8b_1_y6, n8b_1_y7, n8b_adder_1_y0,
       n8b_adder_1_y1, n8b_adder_1_y2, n8b_adder_1_y3, n8b_adder_1_y4, n8b_adder_1_y5, n8b_adder_1_y6,
       n8b_adder_1_y7, n8b_select_1_y0, n8b_select_1_y1, n8b_select_1_y2, n8b_select_1_y3, n8b_select_1_y4,
       n8b_select_1_y5, n8b_select_1_y6, n8b_select_1_y7, n8b_select_2_y0, n8b_select_2_y1, n8b_select_2_y2,
       n8b_select_2_y3, n8b_select_2_y4, n8b_select_2_y5, n8b_select_2_y6, n8b_select_2_y7, n8b_select_3_y0,
       n8b_select_3_y1, n8b_select_3_y2, n8b_select_3_y3, n8b_select_3_y4, n8b_select_3_y5, n8b_select_3_y6,
       n8b_select_3_y7, n8b_select_4_y0, n8b_select_4_y1, n8b_select_4_y2, n8b_select_4_y3, n8b_select_4_y4,
       n8b_select_4_y5, n8b_select_4_y6, n8b_select_4_y7, n8b_select_5_y0, n8b_select_5_y1, n8b_select_5_y2,
       n8b_select_5_y3, n8b_select_5_y4, n8b_select_5_y5, n8b_select_5_y6, n8b_select_5_y7, n7404_1_p2,
       n7404_1_p4, n7404_1_p6, n7404_2_p2, n7404_2_p4, n7404_2_p5, n7404_2_p7, n7404_2_p9, n7404_3_p2,
       n7404_3_p4, n7404_3_p6, n7404_4_p2, n7404_4_p4, n7404_4_p5, n7404_4_p7, n7404_4_p9, n7404_5_p2,
       n7404_5_p4, n7404_5_p6, n7404_6_p2, n7404_6_p4, n7404_6_p5, n7404_6_p7, n7404_6_p9;

  _8b_select u_8b_select_1 (
    .A0(X0), .A1(in_8), .A2(in_9), .A3(in_10), .A4(in_11), .A5(in_12), .A6(in_13), .A7(in_14), .B0(1'b0),
    .B1(1'b0), .B2(1'b0), .B3(1'b0), .B4(1'b0), .B5(1'b0), .B6(1'b0), .B7(1'b0), .S(ZX),
    .Y0(n8b_select_1_y0), .Y1(n8b_select_1_y1), .Y2(n8b_select_1_y2), .Y3(n8b_select_1_y3),
    .Y4(n8b_select_1_y4), .Y5(n8b_select_1_y5), .Y6(n8b_select_1_y6), .Y7(n8b_select_1_y7));
  _8b_select u_8b_select_2 (
    .A0(Y0), .A1(in_16), .A2(in_17), .A3(in_18), .A4(in_19), .A5(in_20), .A6(in_21), .A7(in_22), .B0(1'b0),
    .B1(1'b0), .B2(1'b0), .B3(1'b0), .B4(1'b0), .B5(1'b0), .B6(1'b0), .B7(1'b0), .S(ZY),
    .Y0(n8b_select_2_y0), .Y1(n8b_select_2_y1), .Y2(n8b_select_2_y2), .Y3(n8b_select_2_y3),
    .Y4(n8b_select_2_y4), .Y5(n8b_select_2_y5), .Y6(n8b_select_2_y6), .Y7(n8b_select_2_y7));
  // _7404 7404_1: pin names not known; wires that end beside it: n8b_select_1_y0, n7404_1_p2, n8b_select_1_y1, n7404_1_p4, n8b_select_1_y4, n7404_1_p6, n8b_select_1_y5
  // _7404 7404_2: pin names not known; wires that end beside it: n8b_select_1_y2, n7404_2_p2, n8b_select_1_y3, n7404_2_p4, n7404_2_p5, n8b_select_1_y6, n7404_2_p7, n8b_select_1_y7, n7404_2_p9
  // _7404 7404_3: pin names not known; wires that end beside it: n8b_select_2_y0, n7404_3_p2, n8b_select_2_y1, n7404_3_p4, n8b_select_2_y4, n7404_3_p6, n8b_select_2_y5
  // _7404 7404_4: pin names not known; wires that end beside it: n8b_select_2_y2, n7404_4_p2, n8b_select_2_y3, n7404_4_p4, n7404_4_p5, n8b_select_2_y6, n7404_4_p7, n8b_select_2_y7, n7404_4_p9
  _8b_select u_8b_select_3 (
    .A0(n8b_select_1_y0), .A1(n8b_select_1_y1), .A2(n8b_select_1_y2), .A3(n8b_select_1_y3),
    .A4(n8b_select_1_y4), .A5(n8b_select_1_y5), .A6(n8b_select_1_y6), .A7(n8b_select_1_y7), .B0(n7404_1_p2),
    .B1(n7404_1_p4), .B2(n7404_2_p2), .B3(n7404_2_p4), .B4(n7404_1_p6), .B5(n7404_2_p5), .B6(n7404_2_p7),
    .B7(n7404_2_p9), .S(NX), .Y0(n8b_select_3_y0), .Y1(n8b_select_3_y1), .Y2(n8b_select_3_y2),
    .Y3(n8b_select_3_y3), .Y4(n8b_select_3_y4), .Y5(n8b_select_3_y5), .Y6(n8b_select_3_y6),
    .Y7(n8b_select_3_y7));
  _8b_select u_8b_select_4 (
    .A0(n8b_select_2_y0), .A1(n8b_select_2_y1), .A2(n8b_select_2_y2), .A3(n8b_select_2_y3),
    .A4(n8b_select_2_y4), .A5(n8b_select_2_y5), .A6(n8b_select_2_y6), .A7(n8b_select_2_y7), .B0(n7404_3_p2),
    .B1(n7404_3_p4), .B2(n7404_4_p2), .B3(n7404_4_p4), .B4(n7404_3_p6), .B5(n7404_4_p5), .B6(n7404_4_p7),
    .B7(n7404_4_p9), .S(NY), .Y0(n8b_select_4_y0), .Y1(n8b_select_4_y1), .Y2(n8b_select_4_y2),
    .Y3(n8b_select_4_y3), .Y4(n8b_select_4_y4), .Y5(n8b_select_4_y5), .Y6(n8b_select_4_y6),
    .Y7(n8b_select_4_y7));
  _8b u_8b_1 (
    .A0(n8b_select_3_y0), .A1(n8b_select_3_y1), .A2(n8b_select_3_y2), .A3(n8b_select_3_y3),
    .A4(n8b_select_3_y4), .A5(n8b_select_3_y5), .A6(n8b_select_3_y6), .A7(n8b_select_3_y7),
    .B0(n8b_select_4_y0), .B1(n8b_select_4_y1), .B2(n8b_select_4_y2), .B3(n8b_select_4_y3),
    .B4(n8b_select_4_y4), .B5(n8b_select_4_y5), .B6(n8b_select_4_y6), .B7(n8b_select_4_y7), .Y0(n8b_1_y0),
    .Y1(n8b_1_y1), .Y2(n8b_1_y2), .Y3(n8b_1_y3), .Y4(n8b_1_y4), .Y5(n8b_1_y5), .Y6(n8b_1_y6), .Y7(n8b_1_y7));
  _8b_adder u_8b_adder_1 (
    .A0(n8b_select_3_y0), .A1(n8b_select_3_y1), .A2(n8b_select_3_y2), .A3(n8b_select_3_y3),
    .A4(n8b_select_3_y4), .A5(n8b_select_3_y5), .A6(n8b_select_3_y6), .A7(n8b_select_3_y7),
    .B0(n8b_select_4_y0), .B1(n8b_select_4_y1), .B2(n8b_select_4_y2), .B3(n8b_select_4_y3),
    .B4(n8b_select_4_y4), .B5(n8b_select_4_y5), .B6(n8b_select_4_y6), .B7(n8b_select_4_y7),
    .Y0(n8b_adder_1_y0), .Y1(n8b_adder_1_y1), .Y2(n8b_adder_1_y2), .Y3(n8b_adder_1_y3), .Y4(n8b_adder_1_y4),
    .Y5(n8b_adder_1_y5), .Y6(n8b_adder_1_y6), .Y7(n8b_adder_1_y7));  // open: CO
  _8b_select u_8b_select_5 (
    .A0(n8b_1_y0), .A1(n8b_1_y1), .A2(n8b_1_y2), .A3(n8b_1_y3), .A4(n8b_1_y4), .A5(n8b_1_y5), .A6(n8b_1_y6),
    .A7(n8b_1_y7), .B0(n8b_adder_1_y0), .B1(n8b_adder_1_y1), .B2(n8b_adder_1_y2), .B3(n8b_adder_1_y3),
    .B4(n8b_adder_1_y4), .B5(n8b_adder_1_y5), .B6(n8b_adder_1_y6), .B7(n8b_adder_1_y7), .S(f),
    .Y0(n8b_select_5_y0), .Y1(n8b_select_5_y1), .Y2(n8b_select_5_y2), .Y3(n8b_select_5_y3),
    .Y4(n8b_select_5_y4), .Y5(n8b_select_5_y5), .Y6(n8b_select_5_y6), .Y7(n8b_select_5_y7));
  // _7404 7404_5: pin names not known; wires that end beside it: n8b_select_5_y0, n7404_5_p2, n8b_select_5_y1, n7404_5_p4, n8b_select_5_y4, n7404_5_p6, n8b_select_5_y5
  // _7404 7404_6: pin names not known; wires that end beside it: n8b_select_5_y2, n7404_6_p2, n8b_select_5_y3, n7404_6_p4, n7404_6_p5, n8b_select_5_y6, n7404_6_p7, n8b_select_5_y7, n7404_6_p9
  _8b_select u_8b_select_6 (
    .A0(n8b_select_5_y0), .A1(n8b_select_5_y1), .A2(n8b_select_5_y2), .A3(n8b_select_5_y3),
    .A4(n8b_select_5_y4), .A5(n8b_select_5_y5), .A6(n8b_select_5_y6), .A7(n8b_select_5_y7), .B0(n7404_5_p2),
    .B1(n7404_5_p4), .B2(n7404_6_p2), .B3(n7404_6_p4), .B4(n7404_5_p6), .B5(n7404_6_p5), .B6(n7404_6_p7),
    .B7(n7404_6_p9), .S(NO), .Y0(out_23), .Y1(out_24), .Y2(out_25), .Y3(out_26), .Y4(out_27), .Y5(out_28),
    .Y6(out_29), .Y7(out_30));
endmodule

module _8b (
  input  A0,
  input  A1,
  input  A2,
  input  A3,
  input  A4,
  input  A5,
  input  A6,
  input  A7,
  input  B0,
  input  B1,
  input  B2,
  input  B3,
  input  B4,
  input  B5,
  input  B6,
  input  B7,
  output Y0,
  output Y1,
  output Y2,
  output Y3,
  output Y4,
  output Y5,
  output Y6,
  output Y7
);

  // _7408 7408_1: pin names not known; wires that end beside it: A0, B0, Y0, A1, A4, B4, Y4
  // _7408 7408_2: pin names not known; wires that end beside it: B1, Y1, A2, B2, Y2, A3, B3, Y3, A5, B5, Y5, A6, B6, Y6, A7, B7, Y7
endmodule

module _8b_adder (
  input  A0,
  input  A1,
  input  A2,
  input  A3,
  input  A4,
  input  A5,
  input  A6,
  input  A7,
  input  B0,
  input  B1,
  input  B2,
  input  B3,
  input  B4,
  input  B5,
  input  B6,
  input  B7,
  output Y0,
  output Y1,
  output Y2,
  output Y3,
  output Y4,
  output Y5,
  output Y6,
  output Y7,
  output CO
);

  wire ic_74283_2_p11;

  // IC_74283 ic_74283_1: pin names not known; wires that end beside it: A0, A1, A2, A3, B0, B1, B2, Y0, Y1, Y2, Y3
  // IC_74283 ic_74283_2: pin names not known; wires that end beside it: B3, 1'b0, A4, A5, A6, A7, B4, B5, B6, B7, ic_74283_2_p11, ic_74283_2_p11, Y4, Y5, Y6, Y7, CO
endmodule

module adder (
  input  A,
  input  B,
  input  B_2,
  output Sum,
  output C
);

  wire and_1_out, and_2_out, xor_1_out;

  xor xor_1 (xor_1_out, A, B);
  and and_1 (and_1_out, A, B);
  xor xor_2 (Sum, xor_1_out, B_2);
  and and_2 (and_2_out, xor_1_out, B_2);
  or or_1 (C, and_2_out, and_1_out);
endmodule
